// Logisim project CPU.circ as structural Verilog: 23 circuits, main circuit main
module main (
  input  [3:0] in_1,
  input  in_2,
  input  OE_B,
  output [3:0] MAR_content,
  output [3:0] out_5,
  output [3:0] out_6,
  output [7:0] instruct_Reg_content,
  output [7:0] out_8,
  output [7:0] alu_output,
  output [7:0] reg_A_content,
  output [7:0] reg_B_content,
  output [7:0] output_reg_content
);

  wire clock_1_out, combinedcu_1_o0, combinedcu_1_o1, combinedcu_1_o2, combinedcu_1_o3, combinedcu_1_o4,
       combinedcu_1_o5, combinedcu_1_o6, combinedcu_1_o7, combinedcu_1_o8, combinedcu_1_o9, combinedcu_1_o10,
       combinedcu_1_o11, combinedcu_1_o12, combinedcu_1_o13, combinedcu_1_o14, combinedcu_1_o15,
       delayelement_1_out_2, delayelement_2_out_2, delayelement_3_out_2, outputRegStoredValue_a1,
       outputRegStoredValue_a2, outputRegStoredValue_b1, outputRegStoredValue_b2, outputRegStoredValue_c1,
       outputRegStoredValue_c2, outputRegStoredValue_d1, outputRegStoredValue_d2, outputRegStoredValue_e1,
       outputRegStoredValue_e2, outputRegStoredValue_f1, outputRegStoredValue_f2, outputRegStoredValue_g1,
       outputRegStoredValue_g2, regAstoredValue_a1, regAstoredValue_a2, regAstoredValue_b1,
       regAstoredValue_b2, regAstoredValue_c1, regAstoredValue_c2, regAstoredValue_d1, regAstoredValue_d2,
       regAstoredValue_e1, regAstoredValue_e2, regAstoredValue_f1, regAstoredValue_f2, regAstoredValue_g1,
       regAstoredValue_g2, regBstoredValue_a1, regBstoredValue_a2, regBstoredValue_b1, regBstoredValue_b2,
       regBstoredValue_c1, regBstoredValue_c2, regBstoredValue_d1, regBstoredValue_d2, regBstoredValue_e1,
       regBstoredValue_e2, regBstoredValue_f1, regBstoredValue_f2, regBstoredValue_g1, regBstoredValue_g2,
       undriven;
  wire [3:0] bitselector_1_out, bitselector_3_out, bitselector_4_out, controlled_buffer_1_out, MAR_dout;
  wire [7:0] alu_1_dout, instruction_register_dout, ram_1_dout;

  Clock clock_1 (.out(clock_1_out));
  BitSelector #(.group(4)) bitselector_1 (.in(reg_A_content), .out(bitselector_1_out), .sel(1'b0));
  delayElement delayelement_1 (.in_1(clock_1_out), .out_2(delayelement_1_out_2));
  twoBit7segementDecoder regAstoredValue (
    .in_1(bitselector_1_out), .b1(regAstoredValue_b1), .a1(regAstoredValue_a1), .f1(regAstoredValue_f1),
    .g1(regAstoredValue_g1), .e1(regAstoredValue_e1), .d1(regAstoredValue_d1), .c1(regAstoredValue_c1),
    .b2(regAstoredValue_b2), .a2(regAstoredValue_a2), .f2(regAstoredValue_f2), .g2(regAstoredValue_g2),
    .e2(regAstoredValue_e2), .d2(regAstoredValue_d2), .c2(regAstoredValue_c2));  // open: out_9
  myCounter program_counter (.increment(combinedcu_1_o1), .CLK(delayelement_1_out_2), .out_4(out_6));  // open: INP
  assign controlled_buffer_1_out = combinedcu_1_o0 ? out_6 : 4'bz;  // Controlled_Buffer controlled_buffer_1
  eightbitregister instruction_register (
    .CLK(delayelement_1_out_2), .DIn(alu_1_dout), .WE(combinedcu_1_o7), .OE(combinedcu_1_o8),
    .Dout(instruction_register_dout), .storedData(instruct_Reg_content));
  ALU alu_1 (
    .REGA(reg_A_content), .REGB(reg_B_content), .OE(combinedcu_1_o11), .Dout(alu_1_dout),
    .aluOutput(alu_output));  // open: Cout
  eightbitregister registerA (
    .CLK(delayelement_1_out_2), .DIn(alu_1_dout), .WE(combinedcu_1_o12), .OE(undriven),
    .storedData(reg_A_content));  // open: Dout
  eightbitregister registerB (
    .CLK(delayelement_1_out_2), .DIn(alu_1_dout), .WE(combinedcu_1_o13), .OE(OE_B), .storedData(reg_B_content));  // open: Dout
  BitSelector #(.group(4)) bitselector_2 (.in(instruction_register_dout), .out(controlled_buffer_1_out), .sel(1'b0));
  _7_Segment_Display u_7_segment_display_1 (
    .g(regAstoredValue_g2), .f(regAstoredValue_f2), .a(regAstoredValue_a2), .b(regAstoredValue_b2),
    .e(regAstoredValue_e2), .d(regAstoredValue_d2), .c(regAstoredValue_c2));  // open: dp
  _7_Segment_Display u_7_segment_display_2 (
    .g(regAstoredValue_g1), .f(regAstoredValue_f1), .a(regAstoredValue_a1), .b(regAstoredValue_b1),
    .e(regAstoredValue_e1), .d(regAstoredValue_d1), .c(regAstoredValue_c1));  // open: dp
  LED led_1 (.in(alu_1_dout[7]));
  LED led_2 (.in(alu_1_dout[6]));
  LED led_3 (.in(alu_1_dout[5]));
  LED led_4 (.in(alu_1_dout[4]));
  LED led_5 (.in(alu_1_dout[3]));
  LED led_6 (.in(alu_1_dout[2]));
  LED led_7 (.in(alu_1_dout[1]));
  LED led_8 (.in(alu_1_dout[0]));
  BitSelector #(.group(4)) bitselector_3 (.in(reg_B_content), .out(bitselector_3_out), .sel(1'b0));
  delayElement delayelement_2 (.in_1(delayelement_3_out_2), .out_2(delayelement_2_out_2));
  memoryAddressRegister MAR (
    .CLK(delayelement_1_out_2), .DIn(controlled_buffer_1_out), .WE(combinedcu_1_o9), .OE(combinedcu_1_o10),
    .Dout(MAR_dout), .stored_data(MAR_content));
  assign alu_1_dout = combinedcu_1_o5 ? out_8 : 8'bz;  // Controlled_Buffer controlled_buffer_2
  eightbitregister MBR (
    .CLK(delayelement_2_out_2), .DIn(alu_1_dout), .WE(combinedcu_1_o4), .OE(combinedcu_1_o6),
    .Dout(alu_1_dout), .storedData(out_8));
  delayElement delayelement_3 (.in_1(delayelement_1_out_2), .out_2(delayelement_3_out_2));
  twoBit7segementDecoder regBstoredValue (
    .in_1(bitselector_3_out), .b1(regBstoredValue_b1), .a1(regBstoredValue_a1), .f1(regBstoredValue_f1),
    .g1(regBstoredValue_g1), .e1(regBstoredValue_e1), .d1(regBstoredValue_d1), .c1(regBstoredValue_c1),
    .b2(regBstoredValue_b2), .a2(regBstoredValue_a2), .f2(regBstoredValue_f2), .g2(regBstoredValue_g2),
    .e2(regBstoredValue_e2), .d2(regBstoredValue_d2), .c2(regBstoredValue_c2));  // open: out_9
  assign MAR_dout = in_2 ? in_1 : 4'bz;  // Controlled_Buffer controlled_buffer_3
  eightbitregister output_register (
    .CLK(delayelement_1_out_2), .DIn(alu_1_dout), .WE(combinedcu_1_o15), .OE(combinedcu_1_o14),
    .Dout(alu_1_dout), .storedData(output_reg_content));
  LED led_9 (.in(alu_1_dout[7]));
  LED led_10 (.in(alu_1_dout[6]));
  LED led_11 (.in(alu_1_dout[5]));
  LED led_12 (.in(alu_1_dout[4]));
  LED led_13 (.in(alu_1_dout[3]));
  LED led_14 (.in(alu_1_dout[2]));
  LED led_15 (.in(alu_1_dout[1]));
  LED led_16 (.in(alu_1_dout[0]));
  RAM #(.addrWidth(4)) ram_1 (
    .addr(MAR_dout), .we(combinedcu_1_o2), .oe(combinedcu_1_o3), .clk(delayelement_1_out_2),
    .din(alu_1_dout), .dout(ram_1_dout));
  _7_Segment_Display u_7_segment_display_3 (
    .g(regBstoredValue_g2), .f(regBstoredValue_f2), .a(regBstoredValue_a2), .b(regBstoredValue_b2),
    .e(regBstoredValue_e2), .d(regBstoredValue_d2), .c(regBstoredValue_c2));  // open: dp
  BitSelector #(.group(4)) bitselector_4 (.in(output_reg_content), .out(bitselector_4_out), .sel(1'b0));
  _7_Segment_Display u_7_segment_display_4 (
    .g(regBstoredValue_g1), .f(regBstoredValue_f1), .a(regBstoredValue_a1), .b(regBstoredValue_b1),
    .e(regBstoredValue_e1), .d(regBstoredValue_d1), .c(regBstoredValue_c1));  // open: dp
  assign alu_1_dout = combinedcu_1_o3 ? ram_1_dout : 8'bz;  // Controlled_Buffer controlled_buffer_4
  BitSelector #(.group(4)) bitselector_5 (.in(instruct_Reg_content), .out(out_5), .sel(1'b1));
  twoBit7segementDecoder outputRegStoredValue (
    .in_1(bitselector_4_out), .b1(outputRegStoredValue_b1), .a1(outputRegStoredValue_a1),
    .f1(outputRegStoredValue_f1), .g1(outputRegStoredValue_g1), .e1(outputRegStoredValue_e1),
    .d1(outputRegStoredValue_d1), .c1(outputRegStoredValue_c1), .b2(outputRegStoredValue_b2),
    .a2(outputRegStoredValue_a2), .f2(outputRegStoredValue_f2), .g2(outputRegStoredValue_g2),
    .e2(outputRegStoredValue_e2), .d2(outputRegStoredValue_d2), .c2(outputRegStoredValue_c2));  // open: out_9
  combinedCU combinedcu_1 (
    .a(out_5[0]), .b(out_5[1]), .c(out_5[2]), .d(out_5[3]), .clk(clock_1_out), .o12(combinedcu_1_o12),
    .o9(combinedcu_1_o9), .o15(combinedcu_1_o15), .o14(combinedcu_1_o14), .o11(combinedcu_1_o11),
    .o13(combinedcu_1_o13), .o2(combinedcu_1_o2), .o6(combinedcu_1_o6), .o0(combinedcu_1_o0),
    .o1(combinedcu_1_o1), .o7(combinedcu_1_o7), .o8(combinedcu_1_o8), .o10(combinedcu_1_o10),
    .o4(combinedcu_1_o4), .o5(combinedcu_1_o5), .o3(combinedcu_1_o3));
  _7_Segment_Display u_7_segment_display_5 (
    .g(outputRegStoredValue_g2), .f(outputRegStoredValue_f2), .a(outputRegStoredValue_a2),
    .b(outputRegStoredValue_b2), .e(outputRegStoredValue_e2), .d(outputRegStoredValue_d2),
    .c(outputRegStoredValue_c2));  // open: dp
  _7_Segment_Display u_7_segment_display_6 (
    .g(outputRegStoredValue_g1), .f(outputRegStoredValue_f1), .a(outputRegStoredValue_a1),
    .b(outputRegStoredValue_b1), .e(outputRegStoredValue_e1), .d(outputRegStoredValue_d1),
    .c(outputRegStoredValue_c1));  // open: dp

  // Notes on the sheet:
  //   Note :  this decoder counts upto 15 , so beyound that it will throw error :
  //   internal address bus
  //   internal data bus
  //   external address bus
  //   external data bus
  //   Note:register A and register B are accumulation registers 
  //   opcode are as follows : 1. 0000 - load to reg A 
  //   2. 0001 - load to reg B
  //   3 . 0010 - ADD
  //   4. 0011 - STORE
endmodule

module memory_cell (
  input  DIn,
  input  CLK,
  input  CLR,
  input  WE,
  input  OE,
  output StoredData,
  output Dout
);

  wire and_1_out, and_2_out, not_1_out, or_1_out;

  and and_1 (and_1_out, StoredData, not_1_out);
  not not_1 (not_1_out, WE);
  and and_2 (and_2_out, DIn, WE);
  D_Flip_Flop d_ff_1 (.D(or_1_out), .clk(CLK), .Q(StoredData), .reset(CLR));  // open: Qn, preset
  or or_1 (or_1_out, and_1_out, and_2_out);
  assign Dout = OE ? StoredData : 1'bz;  // Controlled_Buffer controlled_buffer_1
endmodule

module eightbitregister (
  input  CLK,
  input  [7:0] DIn,
  input  WE,
  input  OE,
  output [7:0] Dout,
  output [7:0] storedData
);

  memory_cell memory_cell_1 (
    .DIn(DIn[1]), .CLK(CLK), .WE(WE), .OE(OE), .StoredData(storedData[1]), .Dout(Dout[1]));  // open: CLR
  memory_cell memory_cell_2 (
    .DIn(DIn[2]), .CLK(CLK), .WE(WE), .OE(OE), .StoredData(storedData[2]), .Dout(Dout[2]));  // open: CLR
  memory_cell memory_cell_3 (
    .DIn(DIn[3]), .CLK(CLK), .WE(WE), .OE(OE), .StoredData(storedData[3]), .Dout(Dout[3]));  // open: CLR
  memory_cell memory_cell_4 (
    .DIn(DIn[0]), .CLK(CLK), .WE(WE), .OE(OE), .StoredData(storedData[0]), .Dout(Dout[0]));  // open: CLR
  memory_cell memory_cell_5 (
    .DIn(DIn[4]), .CLK(CLK), .WE(WE), .OE(OE), .StoredData(storedData[4]), .Dout(Dout[4]));  // open: CLR
  memory_cell memory_cell_6 (
    .DIn(DIn[5]), .CLK(CLK), .WE(WE), .OE(OE), .StoredData(storedData[5]), .Dout(Dout[5]));  // open: CLR
  memory_cell memory_cell_7 (
    .DIn(DIn[6]), .CLK(CLK), .WE(WE), .OE(OE), .StoredData(storedData[6]), .Dout(Dout[6]));  // open: CLR
  memory_cell memory_cell_8 (
    .DIn(DIn[7]), .CLK(CLK), .WE(WE), .OE(OE), .StoredData(storedData[7]), .Dout(Dout[7]));  // open: CLR
endmodule

module memoryAddressRegister (
  input  CLK,
  input  [3:0] DIn,
  input  WE,
  input  OE,
  output [3:0] Dout,
  output [3:0] stored_data
);

  memory_cell memory_cell_1 (
    .DIn(DIn[1]), .CLK(CLK), .WE(WE), .OE(OE), .StoredData(stored_data[1]), .Dout(Dout[1]));  // open: CLR
  memory_cell memory_cell_2 (
    .DIn(DIn[2]), .CLK(CLK), .WE(WE), .OE(OE), .StoredData(stored_data[2]), .Dout(Dout[2]));  // open: CLR
  memory_cell memory_cell_3 (
    .DIn(DIn[3]), .CLK(CLK), .WE(WE), .OE(OE), .StoredData(stored_data[3]), .Dout(Dout[3]));  // open: CLR
  memory_cell memory_cell_4 (
    .DIn(DIn[0]), .CLK(CLK), .WE(WE), .OE(OE), .StoredData(stored_data[0]), .Dout(Dout[0]));  // open: CLR
endmodule

module ALU (
  input  [7:0] REGA,
  input  [7:0] REGB,
  input  OE,
  output [7:0] Dout,
  output Cout,
  output [7:0] aluOutput
);

  wire adder_1_cout;

  Adder adder_1 (.a(REGA), .b(REGB), .out(aluOutput), .cout(adder_1_cout));  // open: cin
  assign Dout = OE ? aluOutput : 8'bz;  // Controlled_Buffer controlled_buffer_1
endmodule

module program_counter (
  input  [3:0] in_1,
  input  in_2,
  input  in_3,
  input  WE_MAR,
  input  [7:0] in_5,
  input  count,
  input  OE_MAR,
  input  clr_counter,
  input  in_9,
  input  internal_OE,
  input  WE_RAM,
  input  OE_RAM,
  input  WE_MBR,
  input  in_14,
  input  WE_instruct_reg,
  input  OE_MBR,
  input  OE_instruct_reg,
  input  OE_alu,
  input  WE_A,
  input  OE_A,
  input  WE_O,
  input  OE_O,
  input  WE_B,
  input  OE_B,
  output [3:0] MAR_content,
  output [3:0] out_26,
  output [7:0] instruct_Reg_content,
  output [7:0] out_28,
  output [7:0] alu_output,
  output [7:0] reg_A_content,
  output [7:0] reg_B_content,
  output [7:0] output_reg_content
);

  wire delayelement_1_out_2;
  wire [3:0] bitselector_2_out, controlled_buffer_1_out, MAR_dout;
  wire [7:0] alu_1_dout, instruction_register_dout, ram_1_dout;

  // myCounter program_counter: pin names not known; wires that end beside it: count, in_14, clr_counter, out_26
  assign controlled_buffer_1_out = in_3 ? out_26 : 4'bz;  // Controlled_Buffer controlled_buffer_1
  eightbitregister instruction_register (
    .CLK(in_14), .DIn(alu_1_dout), .WE(WE_instruct_reg), .OE(OE_instruct_reg),
    .Dout(instruction_register_dout), .storedData(instruct_Reg_content));
  ALU alu_1 (
    .REGA(reg_A_content), .REGB(reg_B_content), .OE(OE_alu), .Dout(alu_1_dout), .aluOutput(alu_output));  // open: Cout
  eightbitregister registerA (
    .CLK(in_14), .DIn(alu_1_dout), .WE(WE_A), .OE(OE_A), .storedData(reg_A_content));  // open: Dout
  eightbitregister registerB (
    .CLK(in_14), .DIn(alu_1_dout), .WE(WE_B), .OE(OE_B), .storedData(reg_B_content));  // open: Dout
  BitSelector #(.group(4)) bitselector_1 (.in(instruction_register_dout), .out(controlled_buffer_1_out), .sel(1'b0));
  assign alu_1_dout = in_9 ? in_5 : 8'bz;  // Controlled_Buffer controlled_buffer_2
  LED led_1 (.in(alu_1_dout[7]));
  LED led_2 (.in(alu_1_dout[6]));
  LED led_3 (.in(alu_1_dout[5]));
  LED led_4 (.in(alu_1_dout[4]));
  LED led_5 (.in(alu_1_dout[3]));
  LED led_6 (.in(alu_1_dout[2]));
  LED led_7 (.in(alu_1_dout[1]));
  LED led_8 (.in(alu_1_dout[0]));
  delayElement delayelement_1 (.in_1(in_14), .out_2(delayelement_1_out_2));
  memoryAddressRegister MAR (
    .CLK(delayelement_1_out_2), .DIn(controlled_buffer_1_out), .WE(WE_MAR), .OE(OE_MAR), .Dout(MAR_dout),
    .stored_data(MAR_content));
  assign alu_1_dout = internal_OE ? out_28 : 8'bz;  // Controlled_Buffer controlled_buffer_3
  eightbitregister MBR (
    .CLK(delayelement_1_out_2), .DIn(alu_1_dout), .WE(WE_MBR), .OE(OE_MBR), .Dout(alu_1_dout),
    .storedData(out_28));
  assign MAR_dout = in_2 ? in_1 : 4'bz;  // Controlled_Buffer controlled_buffer_4
  eightbitregister output_register (
    .CLK(in_14), .DIn(alu_1_dout), .WE(WE_O), .OE(OE_O), .Dout(alu_1_dout), .storedData(output_reg_content));
  LED led_9 (.in(alu_1_dout[7]));
  LED led_10 (.in(alu_1_dout[6]));
  LED led_11 (.in(alu_1_dout[5]));
  LED led_12 (.in(alu_1_dout[4]));
  LED led_13 (.in(alu_1_dout[3]));
  LED led_14 (.in(alu_1_dout[2]));
  LED led_15 (.in(alu_1_dout[1]));
  LED led_16 (.in(alu_1_dout[0]));
  RAM #(.addrWidth(4)) ram_1 (
    .addr(MAR_dout), .we(WE_RAM), .oe(OE_RAM), .clk(in_14), .din(alu_1_dout), .dout(ram_1_dout));
  assign alu_1_dout = in_14 ? ram_1_dout : 8'bz;  // Controlled_Buffer controlled_buffer_5
  BitSelector #(.group(4)) bitselector_2 (.in(instruct_Reg_content), .out(bitselector_2_out), .sel(1'b1));
  combinedCU combinedcu_1 (
    .a(bitselector_2_out[0]), .b(bitselector_2_out[1]), .c(bitselector_2_out[2]), .d(bitselector_2_out[3]));  // open: clk, o12, o9, o15, o14, o11, o13, o2, o6, o0, o1, o7, o8, o10, o4, o5, o3

  // Notes on the sheet:
  //   Note:register A and register B are accumulation registers 
  //   opcode are as follows : 1. 0000 - load to reg A 
  //   3 . 0010 - ADD
  //   4. 0011 - STORE
  //   2. 0001 - load to reg B
  //   internal address bus
  //   internal data bus
  //   external address bus
  //   external data bus
endmodule

module myCounter (
  input  [3:0] INP,
  input  increment,
  input  CLK,
  output [3:0] out_4
);

  wire t_ff_1_qn, t_ff_2_qn, t_ff_3_qn;

  T_Flip_Flop t_ff_1 (.T(increment), .clk(CLK), .Q(out_4[0]), .Qn(t_ff_1_qn), .reset(out_4[2]), .preset(INP[0]));
  T_Flip_Flop t_ff_2 (.T(increment), .clk(t_ff_1_qn), .Q(out_4[1]), .Qn(t_ff_2_qn), .reset(out_4[2]), .preset(INP[2]));
  T_Flip_Flop t_ff_3 (.T(increment), .clk(t_ff_2_qn), .Q(out_4[2]), .Qn(t_ff_3_qn), .reset(out_4[2]), .preset(INP[1]));
  T_Flip_Flop t_ff_4 (.T(increment), .clk(t_ff_3_qn), .Q(out_4[3]), .reset(1'b1), .preset(INP[3]));  // open: Qn
endmodule

module myDecoder (
  input  A,
  input  B,
  input  C,
  input  D,
  output o1,
  output o2,
  output o3,
  output o4
);

  wire not_1_out, not_2_out, not_3_out, not_4_out;

  not not_1 (not_1_out, A);
  not not_2 (not_2_out, B);
  not not_3 (not_3_out, C);
  not not_4 (not_4_out, D);
  and and_1 (o1, not_1_out, not_2_out);
  and and_2 (o2, A, not_2_out);
  and and_3 (o3, not_1_out, B);
  and and_4 (o4, A, B);
endmodule

module myMultiplexer (
  input  s1,
  input  s2,
  input  s3,
  output o1,
  output o2,
  output o3,
  output o4,
  output o5,
  output o6
);

  wire and_1_out, and_2_out, and_3_out, and_4_out, and_5_out, and_6_out, not_1_out, not_2_out, not_3_out;

  not not_1 (not_1_out, s1);
  not not_2 (not_2_out, s2);
  not not_3 (not_3_out, s3);
  and and_1 (and_1_out, not_1_out, not_2_out);
  and and_2 (and_2_out, s1, not_2_out);
  and and_3 (and_3_out, not_1_out, s2);
  and and_4 (and_4_out, s1, s2);
  and and_5 (and_5_out, not_1_out, not_2_out);
  and and_6 (and_6_out, s3, not_2_out);
  and and_7 (o1, and_1_out, not_3_out);
  and and_8 (o2, and_2_out, not_3_out);
  and and_9 (o3, and_3_out, not_3_out);
  and and_10 (o4, and_4_out, not_3_out);
  and and_11 (o5, and_5_out, s3);
  and and_12 (o6, and_6_out, s1);
endmodule

module controlUnit (
  input  en,
  input  inc,
  input  clk,
  output [3:0] out_4,
  output d15,
  output d9,
  output d11,
  output d13,
  output d14,
  output d3,
  output d7,
  output d8,
  output d10,
  output d12,
  output d0,
  output d1,
  output d2,
  output d4,
  output d5,
  output d6
);

  wire mydecoder2_1_o0, mydecoder2_1_o1, mydecoder2_1_o2, mydecoder2_1_o3, mydecoder2_1_o4, mydecoder2_1_o5;
  wire [3:0] undriven;

  stepCounter1 stepcounter1_1 (.INP(undriven), .increment(inc), .CLK(clk), .out_4(out_4));
  myDecoder2 mydecoder2_1 (
    .en(en), .s1(out_4[0]), .s2(out_4[1]), .s3(out_4[2]), .o0(mydecoder2_1_o0), .o1(mydecoder2_1_o1),
    .o2(mydecoder2_1_o2), .o3(mydecoder2_1_o3), .o4(mydecoder2_1_o4), .o5(mydecoder2_1_o5));
  or c0 (d0, mydecoder2_1_o0, mydecoder2_1_o0);
  or c1 (d1, mydecoder2_1_o1, mydecoder2_1_o1);
  // OR_Gate c2 has open pins: out=d2
  or c3 (d3, mydecoder2_1_o1, mydecoder2_1_o4);
  or c4 (d4, mydecoder2_1_o1, mydecoder2_1_o4);
  or c5 (d5, mydecoder2_1_o2, mydecoder2_1_o5);
  // OR_Gate c6 has open pins: out=d6
  or c7 (d7, mydecoder2_1_o2, mydecoder2_1_o2);
  or c8 (d8, mydecoder2_1_o3, mydecoder2_1_o3);
  or c9 (d9, mydecoder2_1_o0, mydecoder2_1_o3);
  or c10 (d10, mydecoder2_1_o1, mydecoder2_1_o4);
  // OR_Gate c11 has open pins: out=d11
  or c12 (d12, mydecoder2_1_o5, mydecoder2_1_o5);
  // OR_Gate c13 has open pins: out=d13
  // OR_Gate c14 has open pins: out=d14
  // OR_Gate c15 has open pins: out=d15
endmodule

module myDecoder2 (
  input  en,
  input  s1,
  input  s2,
  input  s3,
  output o0,
  output o1,
  output o2,
  output o3,
  output o4,
  output o5
);

  wire and_1_out, and_2_out, and_3_out, and_4_out, and_5_out, and_6_out, and_7_out, and_8_out, and_9_out,
       and_10_out, and_11_out, and_12_out, not_1_out, not_2_out, not_3_out, not_4_out;

  not not_1 (not_1_out, en);
  not not_2 (not_2_out, s1);
  not not_3 (not_3_out, s2);
  not not_4 (not_4_out, s3);
  and and_1 (and_1_out, not_3_out, en);
  and and_2 (and_2_out, not_3_out, en);
  and and_3 (and_3_out, s2, en);
  and and_4 (and_4_out, s2, en);
  and and_5 (and_5_out, not_3_out, en);
  and and_6 (and_6_out, not_3_out, en);
  and and_7 (and_7_out, not_2_out, and_1_out);
  and and_8 (and_8_out, s1, and_2_out);
  and and_9 (and_9_out, not_2_out, and_3_out);
  and and_10 (and_10_out, s1, and_4_out);
  and and_11 (and_11_out, not_2_out, and_5_out);
  and and_12 (and_12_out, s3, and_6_out);
  and and_13 (o0, and_7_out, not_4_out);
  and and_14 (o1, and_8_out, not_4_out);
  and and_15 (o2, and_9_out, not_4_out);
  and and_16 (o3, and_10_out, not_4_out);
  and and_17 (o4, and_11_out, s3);
  and and_18 (o5, and_12_out, s1);
endmodule

module stepCounter1 (
  input  [3:0] INP,
  input  increment,
  input  CLK,
  output [3:0] out_4
);

  wire and_1_out, t_ff_1_qn, t_ff_2_qn, t_ff_3_qn;

  T_Flip_Flop t_ff_1 (.T(increment), .clk(CLK), .Q(out_4[0]), .Qn(t_ff_1_qn), .reset(and_1_out), .preset(INP[0]));
  T_Flip_Flop t_ff_2 (.T(increment), .clk(t_ff_1_qn), .Q(out_4[1]), .Qn(t_ff_2_qn), .reset(and_1_out), .preset(INP[2]));
  T_Flip_Flop t_ff_3 (.T(increment), .clk(t_ff_2_qn), .Q(out_4[2]), .Qn(t_ff_3_qn), .reset(and_1_out), .preset(INP[1]));
  T_Flip_Flop t_ff_4 (.T(increment), .clk(t_ff_3_qn), .Q(out_4[3]), .reset(and_1_out), .preset(INP[3]));  // open: Qn
  and and_1 (and_1_out, out_4[2], out_4[1]);
endmodule

module controlUnit2 (
  input  en,
  input  inc,
  input  clk,
  output [3:0] out_4,
  output d15,
  output d9,
  output d11,
  output d13,
  output d14,
  output d3,
  output d7,
  output d8,
  output d10,
  output d12,
  output d0,
  output d1,
  output d2,
  output d4,
  output d5,
  output d6
);

  wire mydecoder2_1_o0, mydecoder2_1_o1, mydecoder2_1_o2, mydecoder2_1_o3, mydecoder2_1_o4, mydecoder2_1_o5;
  wire [3:0] undriven;

  stepCounter1 stepcounter1_1 (.INP(undriven), .increment(inc), .CLK(clk), .out_4(out_4));
  myDecoder2 mydecoder2_1 (
    .en(en), .s1(out_4[0]), .s2(out_4[1]), .s3(out_4[2]), .o0(mydecoder2_1_o0), .o1(mydecoder2_1_o1),
    .o2(mydecoder2_1_o2), .o3(mydecoder2_1_o3), .o4(mydecoder2_1_o4), .o5(mydecoder2_1_o5));
  or c0 (d0, mydecoder2_1_o0, mydecoder2_1_o0);
  or c1 (d1, mydecoder2_1_o1, mydecoder2_1_o1);
  // OR_Gate c2 has open pins: out=d2
  or c3 (d3, mydecoder2_1_o1, mydecoder2_1_o4);
  or c4 (d4, mydecoder2_1_o1, mydecoder2_1_o4);
  or c5 (d5, mydecoder2_1_o2, mydecoder2_1_o5);
  // OR_Gate c6 has open pins: out=d6
  or c7 (d7, mydecoder2_1_o2, mydecoder2_1_o2);
  or c8 (d8, mydecoder2_1_o3, mydecoder2_1_o3);
  or c9 (d9, mydecoder2_1_o0, mydecoder2_1_o3);
  or c10 (d10, mydecoder2_1_o1, mydecoder2_1_o4);
  // OR_Gate c11 has open pins: out=d11
  // OR_Gate c12 has open pins: out=d12
  or c13 (d13, mydecoder2_1_o5, mydecoder2_1_o5);
  // OR_Gate c14 has open pins: out=d14
  // OR_Gate c15 has open pins: out=d15
endmodule

module controlUnit3 (
  input  en,
  input  inc,
  input  clk,
  output [3:0] out_4,
  output d15,
  output d9,
  output d11,
  output d13,
  output d14,
  output d3,
  output d7,
  output d8,
  output d10,
  output d12,
  output d0,
  output d1,
  output d2,
  output d4,
  output d5,
  output d6
);

  wire mydecoder2_1_o0, mydecoder2_1_o1, mydecoder2_1_o2, mydecoder2_1_o3;
  wire [3:0] undriven;

  stepCounter1 stepcounter1_1 (.INP(undriven), .increment(inc), .CLK(clk), .out_4(out_4));
  myDecoder2 mydecoder2_1 (
    .en(en), .s1(out_4[0]), .s2(out_4[1]), .s3(out_4[2]), .o0(mydecoder2_1_o0), .o1(mydecoder2_1_o1),
    .o2(mydecoder2_1_o2), .o3(mydecoder2_1_o3));  // open: o4, o5
  or c0 (d0, mydecoder2_1_o0, mydecoder2_1_o0);
  or c1 (d1, mydecoder2_1_o1, mydecoder2_1_o1);
  // OR_Gate c2 has open pins: out=d2
  or c3 (d3, mydecoder2_1_o1, mydecoder2_1_o1);
  or c4 (d4, mydecoder2_1_o1, mydecoder2_1_o1);
  or c5 (d5, mydecoder2_1_o2, mydecoder2_1_o2);
  // OR_Gate c6 has open pins: out=d6
  or c7 (d7, mydecoder2_1_o2, mydecoder2_1_o2);
  // OR_Gate c8 has open pins: out=d8
  or c9 (d9, mydecoder2_1_o0, mydecoder2_1_o0);
  or c10 (d10, mydecoder2_1_o1, mydecoder2_1_o1);
  or c11 (d11, mydecoder2_1_o3, mydecoder2_1_o3);
  // OR_Gate c12 has open pins: out=d12
  // OR_Gate c13 has open pins: out=d13
  // OR_Gate c14 has open pins: out=d14
  or c15 (d15, mydecoder2_1_o3, mydecoder2_1_o3);
endmodule

module stepCounter2 (
  input  [3:0] INP,
  input  increment,
  input  CLK,
  output [3:0] out_4
);

  wire and_1_out, t_ff_1_qn, t_ff_2_qn, t_ff_3_qn;

  T_Flip_Flop t_ff_1 (.T(increment), .clk(CLK), .Q(out_4[0]), .Qn(t_ff_1_qn), .reset(and_1_out), .preset(INP[0]));
  T_Flip_Flop t_ff_2 (.T(increment), .clk(t_ff_1_qn), .Q(out_4[1]), .Qn(t_ff_2_qn), .reset(and_1_out), .preset(INP[2]));
  T_Flip_Flop t_ff_3 (.T(increment), .clk(t_ff_2_qn), .Q(out_4[2]), .Qn(t_ff_3_qn), .reset(and_1_out), .preset(INP[1]));
  T_Flip_Flop t_ff_4 (.T(increment), .clk(t_ff_3_qn), .Q(out_4[3]), .reset(1'b1), .preset(INP[3]));  // open: Qn
  and and_1 (and_1_out, out_4[0], out_4[2]);
endmodule

module controlUnit4 (
  input  en,
  input  inc,
  input  clk,
  output [3:0] out_4,
  output d15,
  output d9,
  output d11,
  output d13,
  output d14,
  output d3,
  output d7,
  output d8,
  output d10,
  output d12,
  output d0,
  output d1,
  output d2,
  output d4,
  output d5,
  output d6
);

  wire mydecoder2_1_o0, mydecoder2_1_o1, mydecoder2_1_o2, mydecoder2_1_o3, mydecoder2_1_o4;
  wire [3:0] undriven;

  stepCounter1 stepcounter1_1 (.INP(undriven), .increment(inc), .CLK(clk), .out_4(out_4));
  myDecoder2 mydecoder2_1 (
    .en(en), .s1(out_4[0]), .s2(out_4[1]), .s3(out_4[2]), .o0(mydecoder2_1_o0), .o1(mydecoder2_1_o1),
    .o2(mydecoder2_1_o2), .o3(mydecoder2_1_o3), .o4(mydecoder2_1_o4));  // open: o5
  or c0 (d0, mydecoder2_1_o0, mydecoder2_1_o0);
  or c1 (d1, mydecoder2_1_o1, mydecoder2_1_o1);
  or c2 (d2, mydecoder2_1_o4, mydecoder2_1_o4);
  or c3 (d3, mydecoder2_1_o1, mydecoder2_1_o1);
  or c4 (d4, mydecoder2_1_o1, mydecoder2_1_o3);
  or c5 (d5, mydecoder2_1_o2, mydecoder2_1_o2);
  or c6 (d6, mydecoder2_1_o4, mydecoder2_1_o4);
  or c7 (d7, mydecoder2_1_o2, mydecoder2_1_o2);
  or c8 (d8, mydecoder2_1_o3, mydecoder2_1_o3);
  or c9 (d9, mydecoder2_1_o0, mydecoder2_1_o3);
  or c10 (d10, mydecoder2_1_o1, mydecoder2_1_o4);
  // OR_Gate c11 has open pins: out=d11
  // OR_Gate c12 has open pins: out=d12
  // OR_Gate c13 has open pins: out=d13
  or c14 (d14, mydecoder2_1_o3, mydecoder2_1_o3);
  // OR_Gate c15 has open pins: out=d15
endmodule

module combinedCU (
  input  a,
  input  b,
  input  c,
  input  d,
  input  clk,
  output o12,
  output o9,
  output o15,
  output o14,
  output o11,
  output o13,
  output o2,
  output o6,
  output o0,
  output o1,
  output o7,
  output o8,
  output o10,
  output o4,
  output o5,
  output o3
);

  wire controlunit2_1_d0, controlunit2_1_d1, controlunit2_1_d3, controlunit2_1_d4, controlunit2_1_d5,
       controlunit2_1_d7, controlunit2_1_d8, controlunit2_1_d9, controlunit2_1_d10, controlunit3_1_d0,
       controlunit3_1_d1, controlunit3_1_d3, controlunit3_1_d4, controlunit3_1_d5, controlunit3_1_d7,
       controlunit3_1_d9, controlunit3_1_d10, controlunit4_1_d0, controlunit4_1_d1, controlunit4_1_d3,
       controlunit4_1_d4, controlunit4_1_d5, controlunit4_1_d7, controlunit4_1_d8, controlunit4_1_d9,
       controlunit4_1_d10, controlunit_1_d0, controlunit_1_d1, controlunit_1_d3, controlunit_1_d4,
       controlunit_1_d5, controlunit_1_d7, controlunit_1_d8, controlunit_1_d9, controlunit_1_d10,
       mydecoder_1_o1, mydecoder_1_o2, mydecoder_1_o3, mydecoder_1_o4;
  wire [3:0] controlunit_1_out_4;

  myDecoder mydecoder_1 (
    .A(a), .B(b), .C(c), .D(d), .o1(mydecoder_1_o1), .o2(mydecoder_1_o2), .o3(mydecoder_1_o3),
    .o4(mydecoder_1_o4));
  controlUnit controlunit_1 (
    .en(mydecoder_1_o1), .inc(1'b1), .clk(clk), .out_4(controlunit_1_out_4), .d9(controlunit_1_d9),
    .d3(controlunit_1_d3), .d7(controlunit_1_d7), .d8(controlunit_1_d8), .d10(controlunit_1_d10), .d12(o12),
    .d0(controlunit_1_d0), .d1(controlunit_1_d1), .d4(controlunit_1_d4), .d5(controlunit_1_d5));  // open: d15, d11, d13, d14, d2, d6
  controlUnit2 controlunit2_1 (
    .en(mydecoder_1_o2), .inc(1'b1), .clk(clk), .d9(controlunit2_1_d9), .d13(o13), .d3(controlunit2_1_d3),
    .d7(controlunit2_1_d7), .d8(controlunit2_1_d8), .d10(controlunit2_1_d10), .d0(controlunit2_1_d0),
    .d1(controlunit2_1_d1), .d4(controlunit2_1_d4), .d5(controlunit2_1_d5));  // open: out_4, d15, d11, d14, d12, d2, d6
  controlUnit3 controlunit3_1 (
    .en(mydecoder_1_o3), .inc(1'b1), .clk(clk), .d15(o15), .d9(controlunit3_1_d9), .d11(o11),
    .d3(controlunit3_1_d3), .d7(controlunit3_1_d7), .d10(controlunit3_1_d10), .d0(controlunit3_1_d0),
    .d1(controlunit3_1_d1), .d4(controlunit3_1_d4), .d5(controlunit3_1_d5));  // open: out_4, d13, d14, d8, d12, d2, d6
  controlUnit4 controlunit4_1 (
    .en(mydecoder_1_o4), .inc(1'b1), .clk(clk), .d9(controlunit4_1_d9), .d14(o14), .d3(controlunit4_1_d3),
    .d7(controlunit4_1_d7), .d8(controlunit4_1_d8), .d10(controlunit4_1_d10), .d0(controlunit4_1_d0),
    .d1(controlunit4_1_d1), .d2(o2), .d4(controlunit4_1_d4), .d5(controlunit4_1_d5), .d6(o6));  // open: out_4, d15, d11, d13, d12
  fourPinORgate fourpinorgate_1 (
    .in_1(controlunit_1_d9), .in_2(controlunit2_1_d9), .in_3(controlunit3_1_d9), .in_4(controlunit4_1_d9),
    .out_5(o9));
  fourPinORgate fourpinorgate_2 (
    .in_1(controlunit_1_d3), .in_2(controlunit2_1_d3), .in_3(controlunit3_1_d3), .in_4(controlunit4_1_d3),
    .out_5(o3));
  fourPinORgate fourpinorgate_3 (
    .in_1(controlunit_1_d7), .in_2(controlunit2_1_d7), .in_3(controlunit3_1_d7), .in_4(controlunit4_1_d7),
    .out_5(o7));
  threebitOR threebitor_1 (.in_1(controlunit_1_d8), .in_2(controlunit2_1_d8), .in_3(controlunit4_1_d8), .out_4(o8));
  fourPinORgate fourpinorgate_4 (
    .in_1(controlunit_1_d10), .in_2(controlunit2_1_d10), .in_3(controlunit3_1_d10),
    .in_4(controlunit4_1_d10), .out_5(o10));
  fourPinORgate fourpinorgate_5 (
    .in_1(controlunit_1_d0), .in_2(controlunit2_1_d0), .in_3(controlunit3_1_d0), .in_4(controlunit4_1_d0),
    .out_5(o0));
  fourPinORgate fourpinorgate_6 (
    .in_1(controlunit_1_d1), .in_2(controlunit2_1_d1), .in_3(controlunit3_1_d1), .in_4(controlunit4_1_d1),
    .out_5(o1));
  fourPinORgate fourpinorgate_7 (
    .in_1(controlunit_1_d4), .in_2(controlunit2_1_d4), .in_3(controlunit3_1_d4), .in_4(controlunit4_1_d4),
    .out_5(o4));
  fourPinORgate fourpinorgate_8 (
    .in_1(controlunit_1_d5), .in_2(controlunit2_1_d5), .in_3(controlunit3_1_d5), .in_4(controlunit4_1_d5),
    .out_5(o5));
endmodule

module fourPinORgate (
  input  in_1,
  input  in_2,
  input  in_3,
  input  in_4,
  output out_5
);

  wire or_1_out, or_2_out;

  or or_1 (or_1_out, in_1, in_2);
  or or_2 (or_2_out, in_3, in_4);
  or or_3 (out_5, or_1_out, or_2_out);
endmodule

module threebitOR (
  input  in_1,
  input  in_2,
  input  in_3,
  output out_4
);

  wire or_1_out;

  or or_1 (or_1_out, in_1, in_2);
  or or_2 (out_4, or_1_out, in_3);
endmodule

module delayElement (
  input  in_1,
  output out_2
);

  wire not_1_out, not_2_out, not_3_out, not_4_out, not_5_out, not_6_out, not_7_out, not_8_out, not_9_out,
       not_10_out, not_11_out, not_12_out, not_13_out, not_14_out, not_15_out, not_16_out, not_17_out,
       not_18_out, not_19_out, not_20_out, not_21_out, not_22_out, not_23_out, not_24_out, not_25_out,
       not_26_out, not_27_out, not_28_out, not_29_out, not_30_out, not_31_out, not_32_out, not_33_out,
       not_34_out, not_35_out, not_36_out, not_37_out, not_38_out, not_39_out, not_40_out, not_41_out,
       not_42_out, not_43_out, not_44_out, not_45_out, not_46_out, not_47_out, not_48_out, not_49_out,
       not_50_out, not_51_out, not_52_out, not_53_out, not_54_out, not_55_out, not_56_out, not_57_out,
       not_58_out, not_59_out, not_60_out, not_61_out, not_62_out, not_63_out, not_64_out, not_65_out,
       not_66_out, not_67_out, not_68_out, not_69_out, not_70_out, not_71_out, not_72_out, not_73_out,
       not_74_out, not_75_out, not_76_out, not_77_out, not_78_out, not_79_out, not_80_out, not_81_out,
       not_82_out, not_83_out, not_84_out, not_85_out, not_86_out, not_87_out, not_88_out, not_89_out,
       not_90_out, not_91_out, not_92_out, not_93_out, not_94_out, not_95_out, not_96_out, not_97_out,
       not_98_out, not_99_out, not_100_out, not_101_out, not_102_out, not_103_out, not_104_out, not_105_out,
       not_106_out, not_107_out, not_108_out, not_109_out, not_110_out, not_111_out, not_112_out,
       not_113_out, not_114_out, not_115_out, not_116_out, not_117_out, not_118_out, not_119_out,
       not_120_out, not_121_out, not_122_out, not_123_out, not_124_out, not_125_out, not_126_out,
       not_127_out, not_128_out, not_129_out, not_130_out, not_131_out, not_132_out, not_133_out,
       not_134_out, not_135_out, not_136_out, not_137_out, not_138_out, not_139_out, not_140_out,
       not_141_out, not_142_out, not_143_out, not_144_out, not_145_out, not_146_out, not_147_out,
       not_148_out, not_149_out, not_150_out, not_151_out, not_152_out, not_153_out, not_154_out,
       not_155_out, not_156_out, not_157_out, not_158_out, not_159_out, not_160_out, not_161_out,
       not_162_out, not_163_out, not_164_out, not_165_out, not_166_out, not_167_out, not_168_out,
       not_169_out, not_170_out, not_171_out, not_172_out, not_173_out, not_174_out, not_175_out,
       not_176_out, not_177_out, not_178_out, not_179_out, not_180_out, not_181_out, not_182_out,
       not_183_out, not_184_out, not_185_out, not_186_out, not_187_out, not_188_out, not_189_out,
       not_190_out, not_191_out, not_192_out, not_193_out, not_194_out, not_195_out, not_196_out,
       not_197_out, not_198_out, not_199_out, not_200_out, not_201_out, not_202_out, not_203_out,
       not_204_out, not_205_out, not_206_out, not_207_out, not_208_out, not_209_out, not_210_out,
       not_211_out, not_212_out, not_213_out, not_214_out, not_215_out, not_216_out, not_217_out,
       not_218_out, not_219_out, not_220_out, not_221_out, not_222_out, not_223_out, not_224_out,
       not_225_out, not_226_out, not_227_out, not_228_out, not_229_out, not_230_out, not_231_out,
       not_232_out, not_233_out, not_234_out, not_235_out, not_236_out, not_237_out, not_238_out,
       not_239_out, not_240_out, not_241_out, not_242_out, not_243_out, not_244_out, not_245_out,
       not_246_out, not_247_out, not_248_out, not_249_out, not_250_out, not_251_out, not_252_out, not_253_out;

  not not_1 (not_1_out, in_1);
  not not_2 (not_2_out, not_234_out);
  not not_3 (not_3_out, not_235_out);
  not not_4 (not_4_out, not_236_out);
  not not_5 (not_5_out, not_242_out);
  not not_6 (not_6_out, not_243_out);
  not not_7 (not_7_out, not_244_out);
  not not_8 (not_8_out, not_246_out);
  not not_9 (not_9_out, not_1_out);
  not not_10 (not_10_out, not_245_out);
  not not_11 (not_11_out, not_247_out);
  not not_12 (not_12_out, not_248_out);
  not not_13 (not_13_out, not_249_out);
  not not_14 (not_14_out, not_250_out);
  not not_15 (not_15_out, not_251_out);
  not not_16 (not_16_out, not_252_out);
  not not_17 (not_17_out, not_253_out);
  not not_18 (not_18_out, not_2_out);
  not not_19 (not_19_out, not_3_out);
  not not_20 (not_20_out, not_4_out);
  not not_21 (not_21_out, not_5_out);
  not not_22 (not_22_out, not_6_out);
  not not_23 (not_23_out, not_7_out);
  not not_24 (not_24_out, not_10_out);
  not not_25 (not_25_out, not_8_out);
  not not_26 (not_26_out, not_11_out);
  not not_27 (not_27_out, not_12_out);
  not not_28 (not_28_out, not_13_out);
  not not_29 (not_29_out, not_14_out);
  not not_30 (not_30_out, not_15_out);
  not not_31 (not_31_out, not_16_out);
  not not_32 (not_32_out, not_9_out);
  not not_33 (not_33_out, not_18_out);
  not not_34 (not_34_out, not_19_out);
  not not_35 (not_35_out, not_17_out);
  not not_36 (not_36_out, not_20_out);
  not not_37 (not_37_out, not_21_out);
  not not_38 (not_38_out, not_22_out);
  not not_39 (not_39_out, not_23_out);
  not not_40 (not_40_out, not_24_out);
  not not_41 (not_41_out, not_25_out);
  not not_42 (not_42_out, not_26_out);
  not not_43 (not_43_out, not_27_out);
  not not_44 (not_44_out, not_28_out);
  not not_45 (not_45_out, not_29_out);
  not not_46 (not_46_out, not_30_out);
  not not_47 (not_47_out, not_31_out);
  not not_48 (not_48_out, not_35_out);
  not not_49 (not_49_out, not_32_out);
  not not_50 (not_50_out, not_33_out);
  not not_51 (not_51_out, not_34_out);
  not not_52 (not_52_out, not_36_out);
  not not_53 (not_53_out, not_37_out);
  not not_54 (not_54_out, not_38_out);
  not not_55 (not_55_out, not_39_out);
  not not_56 (not_56_out, not_40_out);
  not not_57 (not_57_out, not_41_out);
  not not_58 (not_58_out, not_42_out);
  not not_59 (not_59_out, not_43_out);
  not not_60 (not_60_out, not_44_out);
  not not_61 (not_61_out, not_45_out);
  not not_62 (not_62_out, not_46_out);
  not not_63 (not_63_out, not_47_out);
  not not_64 (not_64_out, not_48_out);
  not not_65 (not_65_out, not_49_out);
  not not_66 (not_66_out, not_50_out);
  not not_67 (not_67_out, not_51_out);
  not not_68 (not_68_out, not_52_out);
  not not_69 (not_69_out, not_53_out);
  not not_70 (not_70_out, not_54_out);
  not not_71 (not_71_out, not_55_out);
  not not_72 (not_72_out, not_56_out);
  not not_73 (not_73_out, not_57_out);
  not not_74 (not_74_out, not_58_out);
  not not_75 (not_75_out, not_59_out);
  not not_76 (not_76_out, not_60_out);
  not not_77 (not_77_out, not_61_out);
  not not_78 (not_78_out, not_65_out);
  not not_79 (not_79_out, not_66_out);
  not not_80 (not_80_out, not_67_out);
  not not_81 (not_81_out, not_68_out);
  not not_82 (not_82_out, not_69_out);
  not not_83 (not_83_out, not_70_out);
  not not_84 (not_84_out, not_71_out);
  not not_85 (not_85_out, not_73_out);
  not not_86 (not_86_out, not_62_out);
  not not_87 (not_87_out, not_63_out);
  not not_88 (not_88_out, not_64_out);
  not not_89 (not_89_out, not_72_out);
  not not_90 (not_90_out, not_74_out);
  not not_91 (not_91_out, not_75_out);
  not not_92 (not_92_out, not_76_out);
  not not_93 (not_93_out, not_77_out);
  not not_94 (not_94_out, not_86_out);
  not not_95 (not_95_out, not_87_out);
  not not_96 (not_96_out, not_88_out);
  not not_97 (not_97_out, not_78_out);
  not not_98 (not_98_out, not_79_out);
  not not_99 (not_99_out, not_80_out);
  not not_100 (not_100_out, not_81_out);
  not not_101 (not_101_out, not_82_out);
  not not_102 (not_102_out, not_83_out);
  not not_103 (not_103_out, not_84_out);
  not not_104 (not_104_out, not_85_out);
  not not_105 (not_105_out, not_90_out);
  not not_106 (not_106_out, not_91_out);
  not not_107 (not_107_out, not_92_out);
  not not_108 (not_108_out, not_93_out);
  not not_109 (not_109_out, not_97_out);
  not not_110 (not_110_out, not_94_out);
  not not_111 (not_111_out, not_95_out);
  not not_112 (not_112_out, not_109_out);
  not not_113 (not_113_out, not_98_out);
  not not_114 (not_114_out, not_113_out);
  not not_115 (not_115_out, not_99_out);
  not not_116 (not_116_out, not_115_out);
  not not_117 (not_117_out, not_100_out);
  not not_118 (not_118_out, not_117_out);
  not not_119 (not_119_out, not_101_out);
  not not_120 (not_120_out, not_119_out);
  not not_121 (not_121_out, not_102_out);
  not not_122 (not_122_out, not_121_out);
  not not_123 (not_123_out, not_103_out);
  not not_124 (not_124_out, not_123_out);
  not not_125 (not_125_out, not_89_out);
  not not_126 (not_126_out, not_125_out);
  not not_127 (not_127_out, not_104_out);
  not not_128 (not_128_out, not_127_out);
  not not_129 (not_129_out, not_105_out);
  not not_130 (not_130_out, not_129_out);
  not not_131 (not_131_out, not_106_out);
  not not_132 (not_132_out, not_131_out);
  not not_133 (not_133_out, not_107_out);
  not not_134 (not_134_out, not_108_out);
  not not_135 (not_135_out, not_110_out);
  not not_136 (not_136_out, not_111_out);
  not not_137 (not_137_out, not_112_out);
  not not_138 (not_138_out, not_114_out);
  not not_139 (not_139_out, not_116_out);
  not not_140 (not_140_out, not_133_out);
  not not_141 (not_141_out, not_134_out);
  not not_142 (not_142_out, not_135_out);
  not not_143 (not_143_out, not_136_out);
  not not_144 (not_144_out, not_96_out);
  not not_145 (not_145_out, not_144_out);
  not not_146 (not_146_out, not_118_out);
  not not_147 (not_147_out, not_120_out);
  not not_148 (not_148_out, not_122_out);
  not not_149 (not_149_out, not_124_out);
  not not_150 (not_150_out, not_126_out);
  not not_151 (not_151_out, not_128_out);
  not not_152 (not_152_out, not_130_out);
  not not_153 (not_153_out, not_132_out);
  not not_154 (not_154_out, not_140_out);
  not not_155 (not_155_out, not_141_out);
  not not_156 (not_156_out, not_142_out);
  not not_157 (not_157_out, not_143_out);
  not not_158 (not_158_out, not_145_out);
  not not_159 (not_159_out, not_137_out);
  not not_160 (not_160_out, not_138_out);
  not not_161 (not_161_out, not_139_out);
  not not_162 (not_162_out, not_146_out);
  not not_163 (not_163_out, not_147_out);
  not not_164 (not_164_out, not_148_out);
  not not_165 (not_165_out, not_149_out);
  not not_166 (not_166_out, not_150_out);
  not not_167 (not_167_out, not_151_out);
  not not_168 (not_168_out, not_152_out);
  not not_169 (not_169_out, not_153_out);
  not not_170 (not_170_out, not_154_out);
  not not_171 (not_171_out, not_155_out);
  not not_172 (not_172_out, not_156_out);
  not not_173 (not_173_out, not_157_out);
  not not_174 (not_174_out, not_158_out);
  not not_175 (not_175_out, not_159_out);
  not not_176 (not_176_out, not_160_out);
  not not_177 (not_177_out, not_161_out);
  not not_178 (not_178_out, not_162_out);
  not not_179 (not_179_out, not_163_out);
  not not_180 (not_180_out, not_164_out);
  not not_181 (not_181_out, not_165_out);
  not not_182 (not_182_out, not_166_out);
  not not_183 (not_183_out, not_167_out);
  not not_184 (not_184_out, not_168_out);
  not not_185 (not_185_out, not_169_out);
  not not_186 (not_186_out, not_170_out);
  not not_187 (not_187_out, not_171_out);
  not not_188 (not_188_out, not_175_out);
  not not_189 (not_189_out, not_172_out);
  not not_190 (not_190_out, not_173_out);
  not not_191 (not_191_out, not_174_out);
  not not_192 (not_192_out, not_176_out);
  not not_193 (not_193_out, not_177_out);
  not not_194 (not_194_out, not_178_out);
  not not_195 (not_195_out, not_179_out);
  not not_196 (not_196_out, not_180_out);
  not not_197 (not_197_out, not_181_out);
  not not_198 (not_198_out, not_182_out);
  not not_199 (not_199_out, not_183_out);
  not not_200 (not_200_out, not_184_out);
  not not_201 (not_201_out, not_185_out);
  not not_202 (not_202_out, not_186_out);
  not not_203 (not_203_out, not_187_out);
  not not_204 (not_204_out, not_188_out);
  not not_205 (not_205_out, not_192_out);
  not not_206 (not_206_out, not_193_out);
  not not_207 (not_207_out, not_194_out);
  not not_208 (not_208_out, not_195_out);
  not not_209 (not_209_out, not_196_out);
  not not_210 (not_210_out, not_197_out);
  not not_211 (not_211_out, not_198_out);
  not not_212 (not_212_out, not_199_out);
  not not_213 (not_213_out, not_200_out);
  not not_214 (not_214_out, not_201_out);
  not not_215 (not_215_out, not_189_out);
  not not_216 (not_216_out, not_190_out);
  not not_217 (not_217_out, not_191_out);
  not not_218 (not_218_out, not_202_out);
  not not_219 (not_219_out, not_203_out);
  not not_220 (not_220_out, not_215_out);
  not not_221 (not_221_out, not_216_out);
  not not_222 (not_222_out, not_217_out);
  not not_223 (not_223_out, not_204_out);
  not not_224 (not_224_out, not_205_out);
  not not_225 (not_225_out, not_206_out);
  not not_226 (not_226_out, not_207_out);
  not not_227 (not_227_out, not_208_out);
  not not_228 (not_228_out, not_209_out);
  not not_229 (not_229_out, not_210_out);
  not not_230 (not_230_out, not_211_out);
  not not_231 (not_231_out, not_212_out);
  not not_232 (not_232_out, not_213_out);
  not not_233 (not_233_out, not_214_out);
  not not_234 (not_234_out, not_223_out);
  not not_235 (not_235_out, not_224_out);
  not not_236 (not_236_out, not_225_out);
  not not_237 (not_237_out, not_218_out);
  not not_238 (not_238_out, not_219_out);
  not not_239 (not_239_out, not_220_out);
  not not_240 (not_240_out, not_221_out);
  not not_241 (not_241_out, not_222_out);
  not not_242 (not_242_out, not_226_out);
  not not_243 (not_243_out, not_227_out);
  not not_244 (not_244_out, not_228_out);
  not not_245 (not_245_out, not_229_out);
  not not_246 (not_246_out, not_230_out);
  not not_247 (not_247_out, not_231_out);
  not not_248 (not_248_out, not_232_out);
  not not_249 (not_249_out, not_233_out);
  not not_250 (not_250_out, not_237_out);
  not not_251 (not_251_out, not_238_out);
  not not_252 (not_252_out, not_239_out);
  not not_253 (not_253_out, not_240_out);
  not not_254 (out_2, not_241_out);
endmodule

module sevenSegmentDecoder (
  input  [3:0] in_1,
  output b,
  output a,
  output f,
  output g,
  output e,
  output d,
  output c
);

  wire and_1_out, and_2_out, and_3_out, and_4_out, and_5_out, and_6_out, and_7_out, and_8_out, and_9_out,
       and_10_out, and_11_out, and_12_out, and_13_out, and_14_out, and_15_out, not_1_out, not_2_out,
       not_3_out, not_4_out, threebitand_1_out_4;

  fourPinORgate fourpinorgate_1 (.in_1(and_2_out), .in_2(and_1_out), .in_3(in_1[1]), .in_4(in_1[3]), .out_5(a));
  threebitOR threebitor_1 (.in_1(and_4_out), .in_2(and_3_out), .in_3(not_2_out), .out_4(b));
  not not_1 (not_1_out, in_1[3]);
  not not_2 (not_2_out, in_1[2]);
  not not_3 (not_3_out, in_1[1]);
  not not_4 (not_4_out, in_1[0]);
  and and_1 (and_1_out, in_1[2], in_1[0]);
  and and_2 (and_2_out, not_2_out, not_4_out);
  and and_3 (and_3_out, not_3_out, not_4_out);
  and and_4 (and_4_out, in_1[1], in_1[0]);
  fourPinORgate fourpinorgate_2 (
    .in_1(threebitand_1_out_4), .in_2(and_7_out), .in_3(and_6_out), .in_4(and_5_out), .out_5(d));
  and and_5 (and_5_out, not_2_out, in_1[1]);
  threebitOR threebitor_2 (.in_1(in_1[0]), .in_2(not_3_out), .in_3(in_1[2]), .out_4(c));
  and and_6 (and_6_out, not_2_out, not_4_out);
  and and_7 (and_7_out, not_4_out, in_1[1]);
  threeBitAND threebitand_1 (.in_1(in_1[0]), .in_2(not_3_out), .in_3(in_1[2]), .out_4(threebitand_1_out_4));
  fourPinORgate fourpinorgate_3 (.in_1(and_12_out), .in_2(and_11_out), .in_3(and_10_out), .in_4(in_1[3]), .out_5(f));
  and and_8 (and_8_out, not_2_out, not_4_out);
  and and_9 (and_9_out, not_4_out, in_1[1]);
  or or_1 (e, and_8_out, and_9_out);
  and and_10 (and_10_out, not_3_out, not_4_out);
  and and_11 (and_11_out, in_1[2], not_3_out);
  and and_12 (and_12_out, in_1[2], not_4_out);
  and and_13 (and_13_out, not_2_out, in_1[1]);
  and and_14 (and_14_out, not_3_out, in_1[2]);
  and and_15 (and_15_out, in_1[1], not_4_out);
  fourPinORgate fourpinorgate_4 (.in_1(and_15_out), .in_2(and_14_out), .in_3(and_13_out), .in_4(in_1[3]), .out_5(g));

  // Notes on the sheet:
  //   A
  //   B
  //   C
  //   D
  //   d
  //   e
  //   c
  //   g
  //   b
  //   a
  //   f
endmodule

module threeBitAND (
  input  in_1,
  input  in_2,
  input  in_3,
  output out_4
);

  wire and_1_out;

  and and_1 (and_1_out, in_1, in_2);
  and and_2 (out_4, and_1_out, in_3);
endmodule

module twoBit7segementDecoder (
  input  [3:0] in_1,
  output b1,
  output a1,
  output f1,
  output g1,
  output e1,
  output d1,
  output c1,
  output [7:0] out_9,
  output b2,
  output a2,
  output f2,
  output g2,
  output e2,
  output d2,
  output c2
);

  wire and_1_out, and_2_out;
  wire [2:2] or_1_out;
  wire [3:0] bitselector_1_out, bitselector_2_out;
  wire [7:0] bit_extender_1_out;

  assign bit_extender_1_out = {{4{1'b0}}, in_1};  // Bit_Extender bit_extender_1
  Adder adder_1 (.a(bit_extender_1_out), .b({{5{1'b0}}, {2{or_1_out[2]}}, 1'b0}), .out(out_9));  // open: cin, cout
  and and_1 (and_1_out, in_1[3], in_1[1]);
  BitSelector #(.group(4)) bitselector_1 (.in(out_9), .out(bitselector_1_out), .sel(1'b0));
  BitSelector #(.group(4)) bitselector_2 (.in(out_9), .out(bitselector_2_out), .sel(1'b1));
  or or_1 (or_1_out[2], and_1_out, and_2_out);
  and and_2 (and_2_out, in_1[2], in_1[3]);
  sevenSegmentDecoder sevensegmentdecoder_1 (
    .in_1(bitselector_1_out), .b(b1), .a(a1), .f(f1), .g(g1), .e(e1), .d(d1), .c(c1));
  sevenSegmentDecoder sevensegmentdecoder_2 (
    .in_1(bitselector_2_out), .b(b2), .a(a2), .f(f2), .g(g2), .e(e2), .d(d2), .c(c2));
  _7_Segment_Display u_7_segment_display_1 (.g(g1), .f(f1), .a(a1), .b(b1), .e(e1), .d(d1), .c(c1));  // open: dp
  _7_Segment_Display u_7_segment_display_2 (.g(g2), .f(f2), .a(a2), .b(b2), .e(e2), .d(d2), .c(c2));  // open: dp
endmodule
